# Fritzing sketch FlashRepeat_final (saved by Fritzing 1.0.5)
circuit board: 8.46667cm x 5.64444cm
breadboards: 1

parts:
  Onderdeel1 = Arduino Uno (Rev3)
  LCM1602_IIC1 = LCM1602 IIC [part_number="LCM1602 IIC" chip_label="LCM1602 IIC" package="DIP (Dual Inline) [THT]"]
  LCD1 = LCD screen
  S1 = Pushbutton [package="[THT]"]  # not connected
  J2 = Piezo Speaker
  R9 = Resistor [tolerance=±1% power=0.25W resistance=100k package=THT]
  R10 = Resistor [tolerance=±1% power=0.25W resistance=100k package=THT]
  R11 = Resistor [tolerance=±5% power=0.25W resistance=100k package=THT]
  R12 = Resistor [tolerance=±1% power=0.25W resistance=100k package=THT]
  S5 = Pushbutton [package="[THT]"]
  S6 = Pushbutton [package="[THT]"]
  S7 = Pushbutton [package="[THT]"]
  S8 = Pushbutton [package="[THT]"]
  R13 = Resistor [tolerance=±1% power=0.25W resistance=220 package=THT]
  R14 = Resistor [tolerance=±1% power=0.25W resistance=220 package=THT]
  R15 = Resistor [tolerance=±1% power=0.25W resistance=220 package=THT]
  R16 = Resistor [tolerance=±1% power=0.25W resistance=220 package=THT]
  LED5 = LED - 5mm [color="Red (633nm)" current=0.030A package="5 mm [THT]"]
  LED6 = LED - 5mm [color="Blue (430nm)" current=0.030A package="5 mm [THT]"]
  LED7 = LED - 5mm [color="Yellow (585nm)" current=0.030A package="5 mm [THT]"]
  LED8 = LED - 5mm [color="Green (555nm)" current=0.030A package="5 mm [THT]"]

nets:
  N1: Onderdeel1.A4/SDA, LCM1602_IIC1.SDA
  N2: Onderdeel1.A5/SCL, LCM1602_IIC1.SCL
  N3: Onderdeel1.D8, R15.Pin_0
  N4: Onderdeel1.D9_PWM, R16.Pin_0
  N5: Onderdeel1.D10_PWM/SS, R9.Pin_1, S8.Pin_1, S8.Pin_2
  N6: Onderdeel1.D11_PWM/MOSI, R10.Pin_1, S5.Pin_1, S5.Pin_2
  N7: Onderdeel1.D12/MISO, R11.Pin_1, S6.Pin_1, S6.Pin_2
  N8: Onderdeel1.D13/SCK, R12.Pin_1, S7.Pin_1, S7.Pin_2
  GND: Onderdeel1.GND, LCM1602_IIC1.GND, J2.pin1, R9.Pin_0, R10.Pin_0, R11.Pin_0, R12.Pin_0, LED5.cathode, LED6.cathode, LED7.cathode, LED8.cathode
  N9: Onderdeel1.D3_PWM, J2.pin2
  N10: Onderdeel1.D6_PWM, R13.Pin_0
  N11: Onderdeel1.D7, R14.Pin_0
  5V: Onderdeel1.5V, LCM1602_IIC1.VCC, S5.Pin_3, S5.Pin_4, S6.Pin_3, S6.Pin_4, S7.Pin_3, S7.Pin_4, S8.Pin_3, S8.Pin_4
  VSS: LCM1602_IIC1.VSS, LCD1.VSS
  VDD: LCM1602_IIC1.VDD, LCD1.VDD
  N12: LCM1602_IIC1.V0, LCD1.V0
  N13: LCM1602_IIC1.RS, LCD1.RS
  N14: LCM1602_IIC1.RW, LCD1.R/W
  N15: LCM1602_IIC1.E, LCD1.E
  N16: LCM1602_IIC1.D0, LCD1.DB0
  N17: LCM1602_IIC1.D1, LCD1.DB1
  N18: LCM1602_IIC1.D2, LCD1.DB2
  N19: LCM1602_IIC1.D3, LCD1.DB3
  N20: LCM1602_IIC1.D4, LCD1.DB4
  N21: LCM1602_IIC1.D5, LCD1.DB5
  N22: LCM1602_IIC1.D6, LCD1.DB6
  N23: LCM1602_IIC1.D7, LCD1.DB7
  N24: LCM1602_IIC1.A, LCD1.LED+
  N25: LCM1602_IIC1.K, LCD1.LED-
  N26: LCM1602_IIC1.LED_A, LCM1602_IIC1.LED_B
  N27: R13.Pin_1, LED8.anode
  N28: R14.Pin_1, LED7.anode
  N29: R15.Pin_1, LED5.anode
  N30: R16.Pin_1, LED6.anode

custom parts:
  LCM1602 IIC: I2C-Module to use a 1602 or 2004 LCD on with the wire.h libory Serial LCD Modul

// code stored in the sketch: AnalogReadSerial2LCD_LED.ino
#include <Wire.h>
#include <LiquidCrystal_I2C.h>

LiquidCrystal_I2C lcd(0x27, 16, 2);   // adress and format LCD

const int analogInPin = A0;           // Analog input pin that the potentiometer is attached to
const int analogOutPin = 9;           // Analog output pin that the LED is attached to

int sensorValue = 0;                  // value read from the pot
int outputValue = 0;                  // value output to the PWM (analog out)

void setup() {
  lcd.init();                         // init LCD
  lcd.backlight();
  lcd.home();
  lcd.setCursor(5, 0);                // place static text
  lcd.print("ADC = ");
  lcd.setCursor(15, 0);
  lcd.print("V");
  lcd.setCursor(0, 1);
  lcd.print("LED : ");
  lcd.setCursor(12, 1);
  lcd.print("%");
  Serial.begin(9600);                 // optional serial monitor
}

void loop() {
  int sensorValue = analogRead(analogInPin);          // read analog A0 en store in sensorValue
  float voltValue = 5.0 / 1024.0 * sensorValue;       // calculate volt at analog A0 and store in voltValue
  float percentValue = sensorValue / 1024.0 * 100.0;  // calculate percentage analog A0 and store in percentValue
  outputValue = map(sensorValue, 0, 1023, 0, 255);    // map analog input to analog output and store in outputValue
  analogWrite(analogOutPin, outputValue);             // write outputValue to analogOutPin

  lcd.setCursor(0, 0);                                // set cursor at deserid position
  leadingZeros(sensorValue, 4);                       // print sensorvalue with number of leading-characters (0 or space as specified in function leadingZeros)
  lcd.setCursor(10, 0);                               // set cursor at deserid position
  lcd.print(voltValue);                               // print voltValue
  lcd.setCursor(6, 1);                                // set cursor at deserid position
  lcd.print(percentValue);                            // print percentValue

  Serial.print("sensor = " );                         // print the results to the serial monitor:
  Serial.print(sensorValue);
  Serial.print("\t output = ");
  Serial.print(outputValue);
  Serial.print("\t procent = ");
  Serial.println(percentValue);

  delay(1000);                                        // set delay
}

void leadingZeros( int value, int width) {            // display result with leading characters
  char valueStr[6];                                   // large enough to hold an int
  itoa (value, valueStr, 10);                         // itoa converts int to string
  int len = strlen(valueStr);                         // calculate length of valueStr
  if (len < width) {
    len = width - len;
    while (len--)
      lcd.print(' ');                                 // for leading zeros place '0' between (), for leading spaces place ' ' between ()
  }
  lcd.print(valueStr);
}
