# Fritzing sketch FlashRepeat_m.Buzzer (saved by Fritzing 1.0.5)
breadboards: 1

parts:
  Bauteil1 = Arduino Uno (Rev3)
  S1 = Pushbutton [package="[THT]"]
  S2 = Pushbutton [package="[THT]"]
  S3 = Pushbutton [package="[THT]"]
  S4 = Pushbutton [package="[THT]"]
  R4 = Resistor [tolerance=±1% power=0.25W resistance=100k package=THT]
  R3 = Resistor [tolerance=±5% power=0.25W resistance=100k package=THT]
  R2 = Resistor [tolerance=±1% power=0.25W resistance=100k package=THT]
  R1 = Resistor [tolerance=±1% power=0.25W resistance=100k package=THT]
  R5 = Resistor [tolerance=±1% power=0.25W resistance=220 package=THT]
  R6 = Resistor [tolerance=±1% power=0.25W resistance=220 package=THT]
  R7 = Resistor [tolerance=±1% power=0.25W resistance=220 package=THT]
  R8 = Resistor [tolerance=±1% power=0.25W resistance=220 package=THT]
  LED1 = LED - 5mm [color="Blue (430nm)" current=0.030A package="5 mm [THT]"]
  LED2 = LED - 5mm [color="Red (633nm)" current=0.030A package="5 mm [THT]"]
  LED3 = LED - 5mm [color="Yellow (585nm)" current=0.030A package="5 mm [THT]"]
  LED4 = LED - 5mm [color="Green (555nm)" current=0.030A package="5 mm [THT]"]
  J1 = Piezo Speaker

nets:
  N1: Bauteil1.D8, J1.pin2
  N2: Bauteil1.D10_PWM/SS, S1.Pin_1, S1.Pin_2, R1.Pin_1
  N3: Bauteil1.D11_PWM/MOSI, S4.Pin_1, S4.Pin_2, R2.Pin_1
  N4: Bauteil1.D12/MISO, S3.Pin_1, S3.Pin_2, R3.Pin_1
  N5: Bauteil1.D13/SCK, S2.Pin_1, S2.Pin_2, R4.Pin_1
  N6: Bauteil1.D4, R8.Pin_0
  N7: Bauteil1.D5_PWM, R7.Pin_0
  N8: Bauteil1.D6_PWM, R6.Pin_0
  N9: Bauteil1.D7, R5.Pin_0
  N10: Bauteil1.5V, S1.Pin_3, S1.Pin_4, S2.Pin_3, S2.Pin_4, S3.Pin_3, S3.Pin_4, S4.Pin_3, S4.Pin_4
  N11: Bauteil1.GND, R4.Pin_0, R3.Pin_0, R2.Pin_0, R1.Pin_0, LED1.cathode, LED2.cathode, LED3.cathode, LED4.cathode, J1.pin1
  N12: R5.Pin_1, LED1.anode
  N13: R6.Pin_1, LED2.anode
  N14: R7.Pin_1, LED3.anode
  N15: R8.Pin_1, LED4.anode
